# Fritzing sketch lcd_shield (saved by Fritzing 0.9.3b)
stripboards: 1

parts:
  Bauteil2 = Arduino Uno (Rev3) - ICSP  # not connected
  J3 = female pin header, 6 pins [form="♀ (female)"]  # not connected
  J4 = female pin header, 8 pins [form="♀ (female)"]
  U2 = LCD-16X2 [package=lcd-16x2]  # not connected
  U3 = PIC-ICSP [package=molex-1x6]  # not connected
  J5 = male pin header, 16 pins [form="♂ (male)"]
  J6 = female pin header, 8 pins [form="♀ (female)"]
  U4 = POT [package=pot_alpha_rv16af-20]
  J2 = female pin header, 8 pins [form="♀ (female)"]

nets:
  N1: J4.pin4, J5.pin2
  N2: J4.pin5, J5.pin15, U4.A
  N3: J5.pin1, J5.pin12, J5.pin16, U4.E, J2.pin2
  N4: J5.pin3, J2.pin3
  N5: J5.pin4, J2.pin4
  N6: J5.pin5, J2.pin5
  N7: J5.pin6, J2.pin6
  N8: J5.pin11, J6.pin2
  N9: J5.pin13, J6.pin4
  N10: J5.pin14, U4.S
