# Fritzing sketch lcd_temperatur_licht NUR HEAT-LED (saved by Fritzing 0.9.3b)
breadboards: 1

parts:
  Bauteil1 = Arduino Uno (Rev3)
  LED1 = smd LED [color="Red (633nm)" package="0603 [SMD]"]
  R1 = Resistor [tolerance=±5% resistance=220 package=THT]

nets:
  N1: Bauteil1.D9_PWM, LED1.anode, R1.Pin_0, R1.Pin_1
  N2: Bauteil1.GND, LED1.cathode
