# Fritzing sketch lcd_temperatur_licht NUR LCD-DISPLAY (saved by Fritzing 0.9.3b)
breadboards: 1

parts:
  Bauteil1 = Arduino Uno (Rev3)
  U1 = LCD-16X2 [package=lcd-16x2]  # not connected
  U2 = POT [package=pot_alpha_rv16af-20]

nets:
  N1: Bauteil1.5V, U2.E
  N2: Bauteil1.GND, U2.A
