# Fritzing sketch lcd_temperatur_licht NUR TEMPERATURSENSOR (saved by Fritzing 0.9.3b)
breadboards: 1

parts:
  Bauteil1 = Arduino Uno (Rev3)
  DHT1 = DHT22 Humidity and Temperature Sensor
  R1 = Resistor [tolerance=±5% resistance=220 package=THT]

nets:
  N1: Bauteil1.D2, DHT1.DATA, R1.Pin_1
  5V: Bauteil1.5V, DHT1.VDD, R1.Pin_0
  GND: Bauteil1.GND, DHT1.GND
