# Fritzing sketch nodeMCU_sensors (saved by Fritzing 0.9.3b)
breadboards: 1

parts:
  U1 = NodeMCU V1.0
  DHT1 = DHT22 Humidity and Temperature Sensor
  R1 = Resistor [tolerance=±5% resistance=220 package="2512 [SMD]"]
  Bauteil1 = BH1750
  LED1 = smd LED [color="Red (633nm)" package="0805 [SMD]"]
  S1 = Momentary Switch [package=ksa_sealed_tac_switch]
  R2 = Resistor [tolerance=±5% resistance=10k package="2512 [SMD]"]
  Bauteil2 = SRF05 Ultrasonic Rangefinder

nets:
  N1: U1.D1, DHT1.DATA
  N2: U1.D2, S1.1
  N3: U1.D3, Bauteil2.Trig
  N4: U1.D4, Bauteil2.Echo
  3V3: U1.3V3, DHT1.VDD, Bauteil1.VCC, S1.4
  GND: U1.GND, DHT1.GND, R1.Pin_1, Bauteil1.GND, R2.Pin_1, Bauteil2.GND
  N5: U1.D5, LED1.cathode
  N6: R1.Pin_0, LED1.anode
  N7: S1.2, R2.Pin_0

custom parts:
  NodeMCU V1.0: ESP8266 based NodeMCU
  BH1750: Light Sensor
