# Fritzing sketch nodeMCU_sensors_with_LCD (saved by Fritzing 0.9.3b)
breadboards: 1
stripboards: 1

parts:
  Bauteil3 = SRF05 Ultrasonic Rangefinder
  S2 = Momentary Switch [package=ksa_sealed_tac_switch]
  U2 = NodeMCU V1.0
  DHT2 = DHT22 Humidity and Temperature Sensor
  R3 = Resistor [tolerance=±5% resistance=10k package="2512 [SMD]"]
  U8 = 74HC595 [package="DIP16 [THT]"]
  U9 = LCD-16X2 [package=lcd-16x2_noholes]
  R6 = Rotary Potentiometer (Small) [maximum_resistance=100kΩ package=THT]
  Bauteil5 = BH1750
  J1 = female pin header, 4 pins [form="♀ (female)"]
  J2 = female pin header, 4 pins [form="♀ (female)"]
  U10 = NodeMCU V1.0  # not connected
  J4 = female pin header, 15 pins [form="♀ (female)"]
  J3 = female pin header, 15 pins [form="♀ (female)"]
  Bauteil6 = BH1750  # not connected
  DHT3 = DHT22 Humidity and Temperature Sensor  # not connected
  J5 = female pin header, 4 pins [form="♀ (female)"]  # not connected
  J6 = female pin header, 4 pins [form="♀ (female)"]
  J7 = female pin header, 5 pins [form="♀ (female)"]
  J8 = female pin header, 4 pins [form="♀ (female)"]
  S3 = Momentary Switch [package=ksa_sealed_tac_switch]
  R7 = Resistor [tolerance=±5% resistance=10k package="2512 [SMD]"]
  U11 = 74HC595 [package="DIP16 [THT]"]
  J9 = female pin header, 16 pins [form="♀ (female)"]

nets:
  N1: Bauteil3.VCC, J2.pin4
  N2: Bauteil3.Trig, J2.pin3
  N3: Bauteil3.Echo, J2.pin2
  N4: Bauteil3.GND, J2.pin1
  N5: S2.1, U2.D0
  N6: S2.2, R3.Pin_1
  VDD: S2.4, U2.Vin, DHT2.VDD, U8.MR, U8.VCC, U9.VDD, Bauteil5.VCC, J1.pin4
  N7: U2.D1, DHT2.DATA
  N8: U2.D2, U8.ST_CP
  N9: U2.D3, Bauteil5.SCL
  N10: U2.D4, Bauteil5.SDA
  N11: U2.3V3, U9.A
  GND: U2.GND, DHT2.GND, R3.Pin_0, U8.GND, U8.OE, U9.VSS, U9.R_W, U9.K, Bauteil5.GND, Bauteil5.ADDR, J1.pin1
  N12: U2.D5, U8.SH_CP
  N13: U2.D6, J1.pin3
  N14: U2.D7, U8.DS
  N15: U2.D8, J1.pin2
  N16: U8.Q1, U9.RS
  N17: U8.Q3, U9.E
  N18: U8.Q4, U9.DB4
  N19: U8.Q5, U9.DB5
  N20: U8.Q6, U9.DB6
  N21: U8.Q7, U9.DB7
  N22: U9.VO, R6.wiper
  N23: J4.pin1, J9.pin15
  N24: J4.pin5, J8.pin2
  N25: J4.pin11, J7.pin2
  N26: J4.pin12, J7.pin3
  N27: J4.pin14, J6.pin2
  N28: J4.pin15, S3.1, S3.2, R7.Pin_0
  N29: J3.pin2, J6.pin4, J7.pin1, J7.pin4, J8.pin4, R7.Pin_1, U11.GND, U11.OE, J9.pin1, J9.pin5, J9.pin16
  N30: J6.pin1, J7.pin5, S3.3, S3.4
  N31: U11.Q1, U11.Q2
  N32: U11.Q3, J9.pin6
  N33: U11.Q4, J9.pin11
  N34: U11.Q5, J9.pin12
  N35: U11.Q6, J9.pin13
  N36: U11.Q7, J9.pin14
  N37: U11.MR, U11.VCC

custom parts:
  NodeMCU V1.0: ESP8266 based NodeMCU
  BH1750: Light Sensor
