# Fritzing sketch nodeMCU_shift_LCD (saved by Fritzing 0.9.3b)
breadboards: 1

parts:
  U1 = NodeMCU V1.0
  U3 = 74HC595 [package="DIP16 [THT]"]
  U4 = LCD-16X2 [package=lcd-16x2_noholes]
  R1 = Rotary Potentiometer (Small) [maximum_resistance=100kΩ package=THT]

nets:
  N1: U1.D2, U3.ST_CP
  N2: U1.3V3, U4.A
  N3: U1.GND, U3.OE
  N4: U1.D5, U3.SH_CP
  N5: U1.D7, U3.DS
  N6: U3.Q1, U4.RS
  N7: U3.Q3, U4.E
  N8: U3.Q4, U4.DB4
  N9: U3.Q5, U4.DB5
  N10: U3.Q6, U4.DB6
  N11: U3.Q7, U4.DB7
  GND: U3.GND, U4.VSS, U4.R_W, U4.K, R1.leg2
  N12: U3.MR, U3.VCC
  N13: U4.VDD, R1.leg1
  N14: U4.VO, R1.wiper

custom parts:
  NodeMCU V1.0: ESP8266 based NodeMCU
