# Fritzing sketch nodeMCU_socket (saved by Fritzing 0.9.3b)
stripboards: 2
breadboards: 1

parts:
  U1 = NodeMCU V1.0
  J3 = male pin header, 15 pins [form="♂ (male)"]
  J2 = male pin header, 15 pins [form="♂ (male)"]
  U3 = LCD-16X2 [package=lcd-16x2]
  Umdrehen = 74HC595 [package="DIP16 [THT]"]
  J6 = male pin header, 10 pins [form="♂ (male)"]  # not connected
  J5 = female pin header, 10 pins [form="♀ (female)"]  # not connected
  J7 = male pin header, 10 pins [form="♂ (male)"]  # not connected
  J4 = female pin header, 10 pins [form="♀ (female)"]  # not connected
  U5 = POT [package=pot_alpha_rv16af-20]
  J8 = female pin header, 16 pins [form="♀ (female)"]
  U7 = 74HC595 [package="DIP16 [THT]"]
  U6 = POT [package=pot_alpha_rv16af-20]
  Umdrehen1 = 74HC595 [package="DIP16 [THT]"]
  U8 = NodeMCU V1.0
  U10 = POT [package=pot_alpha_rv16af-20]
  U9 = LCD-16X2 [package=lcd-16x2]

nets:
  N1: U1.D0, J3.pin15
  N2: U1.D1, J3.pin14
  N3: U1.D2, J3.pin13
  N4: U1.D3, J3.pin12
  N5: U1.D4, J3.pin11
  N6: U1.3V3, J3.pin1, J3.pin10, J2.pin5
  N7: U1.GND, J3.pin2, J3.pin9, J2.pin2, J2.pin6
  N8: U1.D5, J3.pin8
  N9: U1.D6, J3.pin7
  N10: U1.D7, J3.pin6
  N11: U1.D8, J3.pin5
  N12: U1.RX, J3.pin4
  N13: U1.TX, J3.pin3
  N14: U1.Vin, J2.pin1
  N15: U1.RST, J2.pin3
  N16: U1.EN, J2.pin4
  N17: U1.CLK, J2.pin7
  N18: U1.SD0, J2.pin8
  N19: U1.CMD, J2.pin9
  N20: U1.SD1, J2.pin10
  N21: U1.SD2, J2.pin11
  N22: U1.SD3, J2.pin12
  N23: U1.RSV#40, J2.pin13
  N24: U1.RSV#41, J2.pin14
  N25: U1.A0, J2.pin15
  N26: U3.VO, U5.S
  N27: U3.RS, Umdrehen.Q1
  N28: U3.E, Umdrehen.Q3
  N29: U3.DB3, U3.DB4, Umdrehen.Q4
  N30: U3.DB5, Umdrehen.Q5
  N31: U3.DB6, Umdrehen.Q6
  N32: U3.DB7, Umdrehen.Q7
  N33: U3.A, U3.K
  N34: J8.pin1, J8.pin5, J8.pin15, U7.VCC
  N35: J8.pin2, U7.Q2, U7.GND, U6.A
  N36: J8.pin3, U6.S
  N37: J8.pin4, U7.Q7'
  N38: J8.pin6, U7.SH_CP
  N39: J8.pin11, U7.ST_CP
  N40: J8.pin12, U7.OE
  N41: J8.pin13, U7.DS
  N42: J8.pin14, U7.Q0
  N43: Umdrehen1.Q1, U9.RS
  N44: Umdrehen1.Q3, U9.E
  N45: Umdrehen1.Q4, U9.DB4
  N46: Umdrehen1.Q5, U9.DB5
  N47: Umdrehen1.Q6, U9.DB6
  N48: Umdrehen1.Q7, U9.DB7
  GND: Umdrehen1.GND, U8.GND, U9.R_W, U9.K
  N49: Umdrehen1.SH_CP, U8.D3
  N50: Umdrehen1.ST_CP, U8.D0
  N51: Umdrehen1.DS, U8.D1
  N52: U8.3V3, U9.A
  N53: U10.A, U9.VDD
  N54: U10.S, U9.VO
  N55: U10.E, U9.VSS

custom parts:
  NodeMCU V1.0: ESP8266 based NodeMCU
