# Fritzing sketch sensor_shield (saved by Fritzing 0.9.3b)

parts:
  Bauteil1 = Adafruit Proto Shield for Arduino Kit - v.5
  DHT1 = DHT22 Humidity and Temperature Sensor  # not connected
  Bauteil2 = BH1750  # not connected
  U1 = ESP8266 WiFi Module [part_number=ESP8266]  # not connected
  J1 = female pin header, 5 pins [form="♀ (female)"]
  J2 = female pin header, 4 pins [form="♀ (female)"]
  J3 = female pin header, 4 pins [form="♀ (female)"]
  J4 = female pin header, 4 pins [form="♀ (female)"]
  R2 = Resistor [tolerance=±5% resistance=220 package=THT]

nets:
  N1: Bauteil1.GND, Bauteil1.P$11#14, Bauteil1.P$8, Bauteil1.1#195, Bauteil1.N$113, Bauteil1.N$175, J1.pin4, J2.pin1, J4.pin4
  N2: Bauteil1.D0, Bauteil1.N$143, J3.pin4
  N3: Bauteil1.D1, Bauteil1.P$5#144, J4.pin1
  N4: Bauteil1.D2, Bauteil1.1#169, Bauteil1.P$5#170, Bauteil1.P$6#171, J2.pin3, R2.Pin_1
  N5: Bauteil1.+5V, Bauteil1.1#189, Bauteil1.P$5#190, Bauteil1.P$6#191, Bauteil1.P$3, Bauteil1.P$5#219, Bauteil1.P$10, Bauteil1.P$11#237, Bauteil1.N$103, Bauteil1.N$133, Bauteil1.N$162, J1.pin5, J2.pin4, J3.pin1, J3.pin3, R2.Pin_0
  N6: Bauteil1.A1, Bauteil1.N$270, J1.pin2
  N7: Bauteil1.A0, Bauteil1.N$271, J1.pin3
  N8: Bauteil1.P$5#147, J4.pin2
  N9: Bauteil1.1#172, J2.pin2
  N10: Bauteil1.N$130, J3.pin2
  N11: Bauteil1.N$140, J4.pin3
  N12: Bauteil1.N$272, J1.pin1

custom parts:
  Adafruit Proto Shield for Arduino Kit - v.5: Arduino prototyping shield designed by Adafruit Industries
  BH1750: Light Sensor
  ESP8266 WiFi Module: Generic WiFi Module based on the ESP8266 with onboard PCB antenna and UART communications
